# Fritzing sketch proyecto_robotica (saved by Fritzing 0.9.10b)
breadboards: 1

parts:
  Keypad4x1 = Keypad Membran 4x4
  Arduino_Nano = Arduino Nano v2.3
  Terminals = Camdenboss CTB0158-4 [part_number=CTB0158-4 package=THT]
  LCD_Screen = LCD1602-I2C
  R1 = Resistor [tolerance=±5% power=0.25 resistance=10k package=THT]
  R2 = Resistor [tolerance=±5% power=0.25 resistance=10k package=THT]
  R3 = Resistor [tolerance=±5% power=0.25 resistance=10k package=THT]
  R4 = Resistor [tolerance=±5% power=0.25 resistance=10k package=THT]
  Terminals_2 = Camdenboss CTB0158-4 [part_number=CTB0158-4 package=THT]

nets:
  N1: Keypad4x1.Pin1, Arduino_Nano.D9
  N2: Keypad4x1.Pin2, Arduino_Nano.D8
  N3: Keypad4x1.Pin3, Arduino_Nano.D7
  N4: Keypad4x1.Pin4, Arduino_Nano.D6
  N5: Keypad4x1.Pin5, Arduino_Nano.D5
  N6: Keypad4x1.Pin6, Arduino_Nano.D4
  N7: Keypad4x1.Pin7, Arduino_Nano.D3
  N8: Keypad4x1.Pin8, Arduino_Nano.D2
  GND: Arduino_Nano.GND, LCD_Screen.GND, R1.Pin_1, R2.Pin_1, R3.Pin_1, R4.Pin_1
  N9: Arduino_Nano.D10, Terminals.pin1
  N10: Arduino_Nano.D11, Terminals.pin2
  N11: Arduino_Nano.D12, Terminals.pin3
  N12: Arduino_Nano.D13, Terminals.pin4
  N13: Arduino_Nano.A5, LCD_Screen.SCL
  N14: Arduino_Nano.A4, LCD_Screen.SDA
  +5V: Arduino_Nano.+5V, LCD_Screen.VCC
  N15: Terminals.terminal_1, Terminals_2.terminal_4
  N16: Terminals.terminal_2, Terminals_2.terminal_3
  N17: Terminals.terminal_3, Terminals_2.terminal_2
  N18: Terminals.terminal_4, Terminals_2.terminal_1
  N19: R1.Pin_0, Terminals_2.pin1
  N20: R2.Pin_0, Terminals_2.pin2
  N21: R3.Pin_0, Terminals_2.pin3
  N22: R4.Pin_0, Terminals_2.pin4

custom parts:
  Keypad Membran 4x4: Membrane Keypad 4x4 Matrix
  LCD1602-I2C: A standard character display, usually with 2x16 characters. Comes in many colors with LCM1602 IIC attached.
